# Fritzing sketch Actividad2 (saved by Fritzing 0.9.3b)
breadboards: 1

parts:
  Componente1 = Arduino Nano (Rev3.0) (ICSP)
  LED1 = 7-SEGMENT-4DIGIT-YOUNGSUN [package=7-segment-4digit-youngsun]

nets:
  N1: Componente1.D2, LED1.G
  N2: Componente1.D3, LED1.C
  N3: Componente1.D5, LED1.D
  N4: Componente1.D6, LED1.E
  N5: Componente1.D7, LED1.B
  N6: Componente1.D8, LED1.DIG2
  N7: Componente1.D9, LED1.DIG3
  N8: Componente1.D10, LED1.F
  N9: Componente1.D11/MOSI, LED1.A
  N10: Componente1.D12/MISO, LED1.DIG4
  N11: Componente1.D13/SCK, LED1.DIG1

// code stored in the sketch: verde.ino
//7 Segmentos de display
int a = 11;
int b = 7;
int c = 3;
int d = 5;
int e = 6;
int f = 10;
int g = 2;
 
// digitoos de Display
int dg1 = 13;
int dg2 = 8;
int dg3 = 9;
int dg4 = 12;


//Punto
int dp=4;


//Velocidad
int vel=1;


//Unidades,decenas, centenas y millares
int mil,cien,dec,uni;


byte segmentos[7] = { a,b,c,d,e,f,g };
byte orden_digitos[4] = { dg1,dg2,dg3,dg4 };
byte digitos[4][4] = { { 0,0,0,1 },
                      { 0,0,1,0 },
                      { 0,1,0,0 },
                      { 1,0,0,0 }
                    };
byte siete_segmentos_digitos[10][7] = { { 1,1,1,1,1,1,0 },  // = 0
                                 { 0,1,1,0,0,0,0 },  // = 1
                                 { 1,1,0,1,1,0,1 },  // = 2
                                 { 1,1,1,1,0,0,1 },  // = 3
                                 { 0,1,1,0,0,1,1 },  // = 4
                                 { 1,0,1,1,0,1,1 },  // = 5
                                 { 1,0,1,1,1,1,1 },  // = 6
                                 { 1,1,1,0,0,0,0 },  // = 7
                                 { 1,1,1,1,1,1,1 },  // = 8
                                 { 1,1,1,0,0,1,1 }   // = 9
                               };
void EscribeDigito(byte digito, byte numero) {
  int secuencia = 0; 
  //Activa número
  ActivarDigito(digito); 
  //digitalWrite(dp,1);//Punto
  //Escribe Numero 
  for (byte i = 0; i < 7; i++){
    digitalWrite(segmentos[secuencia], siete_segmentos_digitos[numero][i]);
    ++secuencia;
  }
}


void ActivarDigito(int x){
  digitalWrite(dg1, HIGH);
  digitalWrite(dg2, HIGH);
  digitalWrite(dg3, HIGH);
  digitalWrite(dg4, HIGH); 
  switch(x){
    case 1: 
      digitalWrite(dg1, LOW); 
      break;
    case 2: 
      digitalWrite(dg2, LOW); 
      break;
    case 3: 
      digitalWrite(dg3, LOW); 
      break;
    default: 
      digitalWrite(dg4, LOW); 
      break;
  }
}
 
void setup(){
  int i; 
  //Inicializar Pines
  for(i=2; i <= 13;i++)     
     pinMode(i,OUTPUT);
} 


 void loop(){
    start();
}


//funcion 0 a 9999
void start(){
    for(mil=0;mil<=9;mil++){
      for(cien=0;cien<=9;cien++){
          for(dec=0;dec<=9;dec++){
               for(uni=0;uni<=9;uni++){
                   EscribeDigito(1, uni);
                   delay(vel);
                   EscribeDigito(2, dec);
                   delay(vel);
                   EscribeDigito(3, cien);
                   delay(vel);
                   EscribeDigito(4, mil);
                   delay(vel);
               } 
          }    
      }
  }
}
