# Fritzing sketch Actividad5 (saved by Fritzing 0.9.3b)
breadboards: 1

parts:
  LCD1 = LCD screen
  Componente1 = Arduino Uno (Rev3)
  R2 = Rotary Potentiometer (Large) [maximum_resistance=100kΩ package=THT]
  R3 = Resistor [tolerance=±5% resistance=220 package="0603 [SMD]"]
  R4 = Resistor [tolerance=±5% resistance=220 package="0603 [SMD]"]
  R5 = Resistor [tolerance=±5% resistance=220 package="0603 [SMD]"]
  LED1 = smd LED [color="Red (633nm)" package="0603 [SMD]"]
  LED2 = smd LED [color="Red (633nm)" package="0603 [SMD]"]
  LED3 = smd LED [color="Red (633nm)" package="0603 [SMD]"]
  S1 = Pushbutton [package="[SMD]"]
  S2 = Pushbutton [package="[SMD]"]
  R6 = Resistor [tolerance=±5% resistance=220 package="0603 [SMD]"]
  R7 = Resistor [tolerance=±5% resistance=220 package="0603 [SMD]"]
  R8 = Resistor [tolerance=±5% resistance=220 package="0603 [SMD]"]

nets:
  VSS: LCD1.VSS, LCD1.R/W, LCD1.LED-, Componente1.GND, R2.leg2, LED1.cathode, LED2.cathode, LED3.cathode, R6.Pin_1, R7.Pin_1
  VDD: LCD1.VDD, Componente1.5V, R2.leg1, R8.Pin_1
  N1: LCD1.V0, R2.wiper
  N2: LCD1.RS, Componente1.D2
  N3: LCD1.E, Componente1.D3_PWM
  N4: LCD1.DB4, Componente1.D4
  N5: LCD1.DB5, Componente1.D5_PWM
  N6: LCD1.DB6, Componente1.D6_PWM
  N7: LCD1.DB7, Componente1.D7
  N8: LCD1.LED+, R8.Pin_0
  N9: Componente1.D8, R4.Pin_1
  N10: Componente1.D9_PWM, R5.Pin_1
  N11: Componente1.D10_PWM/SS, R3.Pin_1
  N12: Componente1.D11_PWM/MOSI, S1.Pin_3, S1.Pin_4, R6.Pin_0
  N13: Componente1.D12/MISO, S2.Pin_3, S2.Pin_4, R7.Pin_0
  N14: Componente1.3V3, S1.Pin_1, S1.Pin_2, S2.Pin_1, S2.Pin_2
  N15: R3.Pin_0, LED3.anode
  N16: R4.Pin_0, LED1.anode
  N17: R5.Pin_0, LED2.anode
