# Fritzing sketch Actividad8 (saved by Fritzing 0.9.3b)
breadboards: 2

parts:
  Componente1 = Arduino Uno (Rev3)
  R1 = Rotary Potentiometer (Small) [maximum_resistance=100kΩ package=THT]
  LED1 = LED - 5mm [color="Red (633nm)" package="5 mm [THT]"]
  Componente2 = Bluetooth HC-05 Macho

nets:
  N1: Componente1.A1, R1.wiper
  GND: Componente1.GND, R1.leg2, LED1.anode, Componente2.GND
  N2: Componente1.D0/RX, Componente2.RXD
  N3: Componente1.D1/TX, Componente2.TXD
  N4: Componente1.D3_PWM, LED1.cathode
  5V: Componente1.5V, R1.leg1, Componente2.VCC
