# Fritzing sketch Actividad3 (saved by Fritzing 0.9.3b)
breadboards: 1

parts:
  Componente1 = Arduino Nano (Rev3.0)
  R1 = Resistor [tolerance=±5% resistance=220 package="2512 [SMD]"]
  R2 = Resistor [tolerance=±5% resistance=220 package="2512 [SMD]"]
  R3 = Resistor [tolerance=±5% resistance=220 package="2512 [SMD]"]
  R4 = Resistor [tolerance=±5% resistance=220 package="2512 [SMD]"]
  S1 = Pushbutton [package="[THT]"]
  U1 = 7-Segment-Display-4-Red [part_number=HS420561K package="7-Segment-4 [THT]"]
  DHT1 = DHT11 Humitidy and Temperature Sensor
  R5 = Resistor [tolerance=±5% resistance=220 package="2512 [SMD]"]
  R6 = Resistor [tolerance=±5% resistance=220 package="2512 [SMD]"]

nets:
  GND: Componente1.GND, DHT1.GND, R6.Pin_1
  N1: Componente1.D2, U1.pin_11
  N2: Componente1.D3, U1.pin7
  N3: Componente1.D4, U1.pin4
  N4: Componente1.D5, U1.pin2
  N5: Componente1.D6, U1.pin1
  N6: Componente1.D7, U1.pin_10
  N7: Componente1.D8, U1.pin5
  N8: Componente1.D9, U1.pin3
  N9: Componente1.D10, R1.Pin_1
  N10: Componente1.D11/MOSI, R5.Pin_1
  N11: Componente1.D12/MISO, R3.Pin_1
  5V: Componente1.5V, DHT1.VDD
  N12: Componente1.A1, R2.Pin_0
  N13: Componente1.A0, S1.Pin_3, S1.Pin_4, R6.Pin_0
  N14: Componente1.3V3, S1.Pin_1, S1.Pin_2
  N15: Componente1.D13/SCK, R4.Pin_1
  N16: R1.Pin_0, U1.pin_12
  N17: R2.Pin_1, DHT1.DATA
  N18: R3.Pin_0, U1.pin8
  N19: R4.Pin_0, U1.pin6
  N20: U1.pin_9, R5.Pin_0

custom parts:
  7-Segment-Display-4-Red: 7-Segment Display 4 digits Red
  DHT11 Humitidy and Temperature Sensor: DHT11 Humidity and Temperature Sensor
