# Fritzing sketch Actividad7 (saved by Fritzing 0.9.3b)
breadboards: 1

parts:
  Componente1 = Arduino Uno (Rev3)
  R1 = Rotary Potentiometer (Small) [maximum_resistance=100kΩ package=THT]
  LED1 = LED - 5mm [color="Red (633nm)" package="5 mm [THT]"]

nets (from the schematic view):
  N1: Componente1.A1, R1.wiper
  N2: Componente1.GND, R1.leg2, LED1.anode
  N3: Componente1.D3_PWM, LED1.cathode
  N4: Componente1.5V, R1.leg1
