# Fritzing sketch practica1 (saved by Fritzing 0.9.3b)
breadboards: 1

parts:
  Componente1 = Arduino Nano (Rev3.0) (ICSP)
  S1 = Pushbutton [package="[THT]"]
  R1 = Resistor [tolerance=±5% resistance=220 package="2010 [SMD]"]
  LED1 = smd LED [color="Red (633nm)" package="0805 [SMD]"]
  R2 = Resistor [tolerance=±5% resistance=220 package="2010 [SMD]"]

nets:
  N1: Componente1.GND, R1.Pin_0, R2.Pin_0
  N2: Componente1.D2, S1.Pin_1, S1.Pin_2, R2.Pin_1
  N3: Componente1.D3, LED1.anode
  N4: Componente1.5V, S1.Pin_3, S1.Pin_4
  N5: R1.Pin_1, LED1.cathode
